// Logisim project V2.circ as structural Verilog: 15 circuits, main circuit x1ADDER
module x1ADDER (
  input  in_1,
  input  in_2,
  input  carry,
  output sum,
  output carryout
);

  wire and_1_out, and_2_out, xor_1_out;

  and and_1 (and_1_out, in_1, in_2);
  xor xor_1 (xor_1_out, in_1, in_2);
  xor xor_2 (sum, xor_1_out, carry);
  or or_1 (carryout, and_1_out, and_2_out);
  and and_2 (and_2_out, xor_1_out, carry);
endmodule

module x4ADDER (
  input  B8,
  input  in_2,
  input  in_3,
  input  B1,
  input  A8,
  input  in_6,
  input  in_7,
  input  A1,
  input  CARRYIN,
  output C8,
  output out_11,
  output out_12,
  output C1,
  output CARRYOUT
);

  wire x1adder_1_carryout, x1adder_2_carryout, x1adder_3_carryout;

  x1ADDER x1adder_1 (.in_1(B1), .in_2(A1), .carry(CARRYIN), .sum(C1), .carryout(x1adder_1_carryout));
  x1ADDER x1adder_2 (.in_1(in_3), .in_2(in_7), .carry(x1adder_1_carryout), .sum(out_12), .carryout(x1adder_2_carryout));
  x1ADDER x1adder_3 (.in_1(in_2), .in_2(in_6), .carry(x1adder_2_carryout), .sum(out_11), .carryout(x1adder_3_carryout));
  x1ADDER x1adder_4 (.in_1(B8), .in_2(A8), .carry(x1adder_3_carryout), .sum(C8), .carryout(CARRYOUT));
endmodule

module x8PLUS_MINUS (
  input  A128,
  input  in_2,
  input  in_3,
  input  in_4,
  input  in_5,
  input  in_6,
  input  in_7,
  input  A1,
  input  PLUS,
  input  MINUS,
  output OVERFLOW,
  output B128,
  output out_13,
  output out_14,
  output out_15,
  output out_16,
  output out_17,
  output out_18,
  output B1
);

  wire x4adder_1_carryout;

  x4ADDER x4adder_1 (
    .B8(in_5), .in_2(in_6), .in_3(in_7), .B1(A1), .A8(MINUS), .in_6(MINUS), .in_7(MINUS), .A1(MINUS),
    .CARRYIN(PLUS), .C8(out_16), .out_11(out_17), .out_12(out_18), .C1(B1), .CARRYOUT(x4adder_1_carryout));
  x4ADDER x4adder_2 (
    .B8(A128), .in_2(in_2), .in_3(in_3), .B1(in_4), .A8(MINUS), .in_6(MINUS), .in_7(MINUS), .A1(MINUS),
    .CARRYIN(x4adder_1_carryout), .C8(B128), .out_11(out_13), .out_12(out_14), .C1(out_15),
    .CARRYOUT(OVERFLOW));
endmodule

module x16PLUS_MINUS (
  input  A65536,
  input  in_2,
  input  in_3,
  input  in_4,
  input  in_5,
  input  in_6,
  input  in_7,
  input  A256,
  input  A128,
  input  in_10,
  input  in_11,
  input  in_12,
  input  in_13,
  input  in_14,
  input  in_15,
  input  A1,
  input  PLUS,
  input  MINUS,
  output OVERFLOW,
  output b65525,
  output out_21,
  output out_22,
  output out_23,
  output out_24,
  output out_25,
  output out_26,
  output b256,
  output B128,
  output out_29,
  output out_30,
  output out_31,
  output out_32,
  output out_33,
  output out_34,
  output B1
);

  wire x4adder_1_carryout, x4adder_2_carryout, x4adder_3_carryout;

  x4ADDER x4adder_1 (
    .B8(in_13), .in_2(in_14), .in_3(in_15), .B1(A1), .A8(MINUS), .in_6(MINUS), .in_7(MINUS), .A1(MINUS),
    .CARRYIN(PLUS), .C8(out_32), .out_11(out_33), .out_12(out_34), .C1(B1), .CARRYOUT(x4adder_1_carryout));
  x4ADDER x4adder_2 (
    .B8(A128), .in_2(in_10), .in_3(in_11), .B1(in_12), .A8(MINUS), .in_6(MINUS), .in_7(MINUS), .A1(MINUS),
    .CARRYIN(x4adder_1_carryout), .C8(B128), .out_11(out_29), .out_12(out_30), .C1(out_31),
    .CARRYOUT(x4adder_2_carryout));
  x4ADDER x4adder_3 (
    .B8(in_5), .in_2(in_6), .in_3(in_7), .B1(A256), .A8(MINUS), .in_6(MINUS), .in_7(MINUS), .A1(MINUS),
    .CARRYIN(x4adder_2_carryout), .C8(out_24), .out_11(out_25), .out_12(out_26), .C1(b256),
    .CARRYOUT(x4adder_3_carryout));
  x4ADDER x4adder_4 (
    .B8(A65536), .in_2(in_2), .in_3(in_3), .B1(in_4), .A8(MINUS), .in_6(MINUS), .in_7(MINUS), .A1(MINUS),
    .CARRYIN(x4adder_3_carryout), .C8(b65525), .out_11(out_21), .out_12(out_22), .C1(out_23),
    .CARRYOUT(OVERFLOW));
endmodule

module x8COUNTER (
  input  in_1,
  input  in_2,
  input  in_3,
  input  in_4,
  input  in_5,
  input  in_6,
  input  in_7,
  input  in_8,
  input  UPDATE,
  output out_10,
  output out_11,
  output out_12,
  output out_13,
  output out_14,
  output out_15,
  output out_16,
  output out_17
);

  D_Flip_Flop d_ff_1 (.D(in_1), .clk(UPDATE), .Q(out_10));  // open: Qn, preset, reset
  D_Flip_Flop d_ff_2 (.D(in_3), .clk(UPDATE), .Q(out_12));  // open: Qn, preset, reset
  D_Flip_Flop d_ff_3 (.D(in_5), .clk(UPDATE), .Q(out_14));  // open: Qn, preset, reset
  D_Flip_Flop d_ff_4 (.D(in_7), .clk(UPDATE), .Q(out_16));  // open: Qn, preset, reset
  D_Flip_Flop d_ff_5 (.D(in_2), .clk(UPDATE), .Q(out_11));  // open: Qn, preset, reset
  D_Flip_Flop d_ff_6 (.D(in_4), .clk(UPDATE), .Q(out_13));  // open: Qn, preset, reset
  D_Flip_Flop d_ff_7 (.D(in_6), .clk(UPDATE), .Q(out_15));  // open: Qn, preset, reset
  D_Flip_Flop d_ff_8 (.D(in_8), .clk(UPDATE), .Q(out_17));  // open: Qn, preset, reset
endmodule

module x16COUNTER (
  input  in_1,
  input  in_2,
  input  in_3,
  input  in_4,
  input  in_5,
  input  in_6,
  input  in_7,
  input  in_8,
  input  in_9,
  input  in_10,
  input  in_11,
  input  in_12,
  input  in_13,
  input  in_14,
  input  in_15,
  input  in_16,
  input  RESET,
  output out_18,
  output out_19,
  output out_20,
  output out_21,
  output out_22,
  output out_23,
  output out_24,
  output out_25,
  output out_26,
  output out_27,
  output out_28,
  output out_29,
  output out_30,
  output out_31,
  output out_32,
  output out_33
);

  D_Flip_Flop d_ff_1 (.D(in_13), .clk(RESET), .Q(out_30));  // open: Qn, preset, reset
  D_Flip_Flop d_ff_2 (.D(in_14), .clk(RESET), .Q(out_31));  // open: Qn, preset, reset
  D_Flip_Flop d_ff_3 (.D(in_15), .clk(RESET), .Q(out_32));  // open: Qn, preset, reset
  D_Flip_Flop d_ff_4 (.D(in_16), .clk(RESET), .Q(out_33));  // open: Qn, preset, reset
  D_Flip_Flop d_ff_5 (.D(in_9), .clk(RESET), .Q(out_26));  // open: Qn, preset, reset
  D_Flip_Flop d_ff_6 (.D(in_10), .clk(RESET), .Q(out_27));  // open: Qn, preset, reset
  D_Flip_Flop d_ff_7 (.D(in_11), .clk(RESET), .Q(out_28));  // open: Qn, preset, reset
  D_Flip_Flop d_ff_8 (.D(in_12), .clk(RESET), .Q(out_29));  // open: Qn, preset, reset
  D_Flip_Flop d_ff_9 (.D(in_5), .clk(RESET), .Q(out_22));  // open: Qn, preset, reset
  D_Flip_Flop d_ff_10 (.D(in_6), .clk(RESET), .Q(out_23));  // open: Qn, preset, reset
  D_Flip_Flop d_ff_11 (.D(in_7), .clk(RESET), .Q(out_24));  // open: Qn, preset, reset
  D_Flip_Flop d_ff_12 (.D(in_8), .clk(RESET), .Q(out_25));  // open: Qn, preset, reset
  D_Flip_Flop d_ff_13 (.D(in_1), .clk(RESET), .Q(out_18));  // open: Qn, preset, reset
  D_Flip_Flop d_ff_14 (.D(in_2), .clk(RESET), .Q(out_19));  // open: Qn, preset, reset
  D_Flip_Flop d_ff_15 (.D(in_3), .clk(RESET), .Q(out_20));  // open: Qn, preset, reset
  D_Flip_Flop d_ff_16 (.D(in_4), .clk(RESET), .Q(out_21));  // open: Qn, preset, reset
endmodule

module BRACKET_COUNTER (
  input  UPDATE,
  input  MORE,
  input  LESS,
  output B128,
  output out_5,
  output out_6,
  output out_7,
  output out_8,
  output out_9,
  output out_10,
  output B1,
  output OVERFLOW
);

  wire [7:0] x8plus_minus_1_b128;

  x8COUNTER x8counter_1 (
    .in_1(x8plus_minus_1_b128[0]), .in_2(x8plus_minus_1_b128[1]), .in_3(x8plus_minus_1_b128[2]),
    .in_4(x8plus_minus_1_b128[3]), .in_5(x8plus_minus_1_b128[4]), .in_6(x8plus_minus_1_b128[5]),
    .in_7(x8plus_minus_1_b128[6]), .in_8(x8plus_minus_1_b128[7]), .UPDATE(UPDATE), .out_10(B128),
    .out_11(out_5), .out_12(out_6), .out_13(out_7), .out_14(out_8), .out_15(out_9), .out_16(out_10),
    .out_17(B1));
  LED led_1 (.in(B128));
  LED led_2 (.in(out_5));
  LED led_3 (.in(out_6));
  LED led_4 (.in(out_7));
  LED led_5 (.in(out_8));
  LED led_6 (.in(out_9));
  LED led_7 (.in(out_10));
  LED led_8 (.in(B1));
  x8PLUS_MINUS x8plus_minus_1 (
    .A128(B128), .in_2(out_5), .in_3(out_6), .in_4(out_7), .in_5(out_8), .in_6(out_9), .in_7(out_10),
    .A1(B1), .PLUS(MORE), .MINUS(LESS), .OVERFLOW(OVERFLOW), .B128(x8plus_minus_1_b128[0]),
    .out_13(x8plus_minus_1_b128[1]), .out_14(x8plus_minus_1_b128[2]), .out_15(x8plus_minus_1_b128[3]),
    .out_16(x8plus_minus_1_b128[4]), .out_17(x8plus_minus_1_b128[5]), .out_18(x8plus_minus_1_b128[6]),
    .B1(x8plus_minus_1_b128[7]));
  LED led_9 (.in(x8plus_minus_1_b128[0]));
  LED led_10 (.in(x8plus_minus_1_b128[1]));
  LED led_11 (.in(x8plus_minus_1_b128[2]));
  LED led_12 (.in(x8plus_minus_1_b128[3]));
  LED led_13 (.in(x8plus_minus_1_b128[4]));
  LED led_14 (.in(x8plus_minus_1_b128[5]));
  LED led_15 (.in(x8plus_minus_1_b128[6]));
  LED led_16 (.in(x8plus_minus_1_b128[7]));
endmodule

module BRACKET_CHECK (
  input  A128,
  input  in_2,
  input  in_3,
  input  in_4,
  input  in_5,
  input  in_6,
  input  in_7,
  input  A1,
  input  FORWARD_if1,
  output YES,
  output SKIP
);

  wire not_1_out, or_1_out, or_2_out, or_3_out, or_4_out, or_5_out, or_6_out, or_7_out;

  or or_1 (or_1_out, A128, in_2);
  or or_2 (or_2_out, in_3, in_4);
  or or_3 (or_3_out, in_5, in_6);
  or or_4 (or_4_out, in_7, A1);
  or or_5 (or_5_out, or_1_out, or_2_out);
  or or_6 (or_6_out, or_3_out, or_4_out);
  not not_1 (not_1_out, FORWARD_if1);
  or or_7 (or_7_out, or_5_out, or_6_out);
  xnor xnor_1 (YES, or_7_out, not_1_out);
  not not_2 (SKIP, YES);
endmodule

module BRACKET_LOGIC (
  input  UPDATE,
  input  MORE,
  input  LESS,
  output VALID
);

  wire bracket_counter_1_b1, bracket_counter_1_b128, bracket_counter_1_out_5, bracket_counter_1_out_6,
       bracket_counter_1_out_7, bracket_counter_1_out_8, bracket_counter_1_out_9, bracket_counter_1_out_10;

  BRACKET_COUNTER bracket_counter_1 (
    .UPDATE(UPDATE), .MORE(MORE), .LESS(LESS), .B128(bracket_counter_1_b128),
    .out_5(bracket_counter_1_out_5), .out_6(bracket_counter_1_out_6), .out_7(bracket_counter_1_out_7),
    .out_8(bracket_counter_1_out_8), .out_9(bracket_counter_1_out_9), .out_10(bracket_counter_1_out_10),
    .B1(bracket_counter_1_b1));  // open: OVERFLOW
  NULL_CHECK null_check_1 (
    .in_1(bracket_counter_1_b128), .in_2(bracket_counter_1_out_5), .in_3(bracket_counter_1_out_6),
    .in_4(bracket_counter_1_out_7), .in_5(bracket_counter_1_out_8), .in_6(bracket_counter_1_out_9),
    .in_7(bracket_counter_1_out_10), .in_8(bracket_counter_1_b1), .out_9(VALID));
endmodule

module NULL_CHECK (
  input  in_1,
  input  in_2,
  input  in_3,
  input  in_4,
  input  in_5,
  input  in_6,
  input  in_7,
  input  in_8,
  output out_9
);

  wire or_1_out, or_2_out, or_3_out, or_4_out, or_5_out, or_6_out, or_7_out;

  or or_1 (or_1_out, in_1, in_2);
  or or_2 (or_2_out, in_3, in_4);
  or or_3 (or_3_out, in_5, in_6);
  or or_4 (or_4_out, in_7, in_8);
  or or_5 (or_5_out, or_1_out, or_2_out);
  or or_6 (or_6_out, or_3_out, or_4_out);
  or or_7 (or_7_out, or_5_out, or_6_out);
  not not_1 (out_9, or_7_out);
endmodule

module ADRESSE_MAP (
  input  NEXT_CELL,
  input  PREVIOUS_CELL,
  input  UPDATE,
  output B65536,
  output out_5,
  output out_6,
  output out_7,
  output out_8,
  output out_9,
  output out_10,
  output out_11,
  output out_12,
  output out_13,
  output out_14,
  output out_15,
  output out_16,
  output out_17,
  output out_18,
  output B1,
  output OVERFLOW
);

  wire [15:0] x16plus_minus_1_b65525;

  x16COUNTER x16counter_1 (
    .in_1(x16plus_minus_1_b65525[0]), .in_2(x16plus_minus_1_b65525[1]), .in_3(x16plus_minus_1_b65525[2]),
    .in_4(x16plus_minus_1_b65525[3]), .in_5(x16plus_minus_1_b65525[4]), .in_6(x16plus_minus_1_b65525[5]),
    .in_7(x16plus_minus_1_b65525[6]), .in_8(x16plus_minus_1_b65525[7]), .in_9(x16plus_minus_1_b65525[8]),
    .in_10(x16plus_minus_1_b65525[9]), .in_11(x16plus_minus_1_b65525[10]),
    .in_12(x16plus_minus_1_b65525[11]), .in_13(x16plus_minus_1_b65525[12]),
    .in_14(x16plus_minus_1_b65525[13]), .in_15(x16plus_minus_1_b65525[14]),
    .in_16(x16plus_minus_1_b65525[15]), .RESET(UPDATE), .out_18(B65536), .out_19(out_5), .out_20(out_6),
    .out_21(out_7), .out_22(out_8), .out_23(out_9), .out_24(out_10), .out_25(out_11), .out_26(out_12),
    .out_27(out_13), .out_28(out_14), .out_29(out_15), .out_30(out_16), .out_31(out_17), .out_32(out_18),
    .out_33(B1));
  LED led_1 (.in(B65536));
  LED led_2 (.in(out_5));
  LED led_3 (.in(out_6));
  LED led_4 (.in(out_7));
  LED led_5 (.in(out_8));
  LED led_6 (.in(out_9));
  LED led_7 (.in(out_10));
  LED led_8 (.in(out_11));
  LED led_9 (.in(out_12));
  LED led_10 (.in(out_13));
  LED led_11 (.in(out_14));
  LED led_12 (.in(out_15));
  LED led_13 (.in(out_16));
  LED led_14 (.in(out_17));
  LED led_15 (.in(out_18));
  LED led_16 (.in(B1));
  x16PLUS_MINUS x16plus_minus_1 (
    .A65536(B65536), .in_2(out_5), .in_3(out_6), .in_4(out_7), .in_5(out_8), .in_6(out_9), .in_7(out_10),
    .A256(out_11), .A128(out_12), .in_10(out_13), .in_11(out_14), .in_12(out_15), .in_13(out_16),
    .in_14(out_17), .in_15(out_18), .A1(B1), .PLUS(NEXT_CELL), .MINUS(PREVIOUS_CELL), .OVERFLOW(OVERFLOW),
    .b65525(x16plus_minus_1_b65525[0]), .out_21(x16plus_minus_1_b65525[1]),
    .out_22(x16plus_minus_1_b65525[2]), .out_23(x16plus_minus_1_b65525[3]),
    .out_24(x16plus_minus_1_b65525[4]), .out_25(x16plus_minus_1_b65525[5]),
    .out_26(x16plus_minus_1_b65525[6]), .b256(x16plus_minus_1_b65525[7]), .B128(x16plus_minus_1_b65525[8]),
    .out_29(x16plus_minus_1_b65525[9]), .out_30(x16plus_minus_1_b65525[10]),
    .out_31(x16plus_minus_1_b65525[11]), .out_32(x16plus_minus_1_b65525[12]),
    .out_33(x16plus_minus_1_b65525[13]), .out_34(x16plus_minus_1_b65525[14]), .B1(x16plus_minus_1_b65525[15]));
  LED led_17 (.in(x16plus_minus_1_b65525[0]));
  LED led_18 (.in(x16plus_minus_1_b65525[1]));
  LED led_19 (.in(x16plus_minus_1_b65525[2]));
  LED led_20 (.in(x16plus_minus_1_b65525[3]));
  LED led_21 (.in(x16plus_minus_1_b65525[4]));
  LED led_22 (.in(x16plus_minus_1_b65525[5]));
  LED led_23 (.in(x16plus_minus_1_b65525[6]));
  LED led_24 (.in(x16plus_minus_1_b65525[7]));
  LED led_25 (.in(x16plus_minus_1_b65525[8]));
  LED led_26 (.in(x16plus_minus_1_b65525[9]));
  LED led_27 (.in(x16plus_minus_1_b65525[10]));
  LED led_28 (.in(x16plus_minus_1_b65525[11]));
  LED led_29 (.in(x16plus_minus_1_b65525[12]));
  LED led_30 (.in(x16plus_minus_1_b65525[13]));
  LED led_31 (.in(x16plus_minus_1_b65525[14]));
  LED led_32 (.in(x16plus_minus_1_b65525[15]));
endmodule

module ROM_ARCHI (
  input  NEXTINS,
  input  UPDATE,
  input  PREVIOUSINS,
  output INS1,
  output INS2,
  output INS3
);

  wire [15:0] adresse_map_1_b1;

  ADRESSE_MAP adresse_map_1 (
    .NEXT_CELL(NEXTINS), .PREVIOUS_CELL(PREVIOUSINS), .UPDATE(UPDATE), .B65536(adresse_map_1_b1[15]),
    .out_5(adresse_map_1_b1[14]), .out_6(adresse_map_1_b1[13]), .out_7(adresse_map_1_b1[12]),
    .out_8(adresse_map_1_b1[11]), .out_9(adresse_map_1_b1[10]), .out_10(adresse_map_1_b1[9]),
    .out_11(adresse_map_1_b1[8]), .out_12(adresse_map_1_b1[7]), .out_13(adresse_map_1_b1[6]),
    .out_14(adresse_map_1_b1[5]), .out_15(adresse_map_1_b1[4]), .out_16(adresse_map_1_b1[3]),
    .out_17(adresse_map_1_b1[2]), .out_18(adresse_map_1_b1[1]), .B1(adresse_map_1_b1[0]));  // open: OVERFLOW
  ROM #(.addrWidth(16), .dataWidth(3)) rom_1 (.addr(adresse_map_1_b1), .data({INS3, INS2, INS1}));

  // Notes on the sheet:
  //   000
  //   +
  //   001
  //   -
  //   010
  //   >
  //   011
  //   <
  //   .
  //   100
  //   ,
  //   101
  //   [
  //   110
  //   ]
  //   111
  //   contents of rom_1 (hex, n*v repeats v):
  //   6 0 0 7 2 2
endmodule

module RAM_ARCHI (
  input  READ,
  input  NEXTCELL,
  input  PREVCELL,
  input  RESETTONULL,
  input  UPDATEREGS,
  input  UPDATERAM,
  input  RESETTO0,
  input  A65355,
  input  in_9,
  input  in_10,
  input  in_11,
  input  in_12,
  input  in_13,
  input  in_14,
  input  A1,
  input  PLUS,
  input  MINUS,
  input  WRITE,
  output B128,
  output out_20,
  output out_21,
  output out_22,
  output out_23,
  output out_24,
  output out_25,
  output B1,
  output READED
);

  wire not_1_out, not_2_out, not_4_out, or_1_out, x8plus_minus_1_b1, x8plus_minus_1_b128,
       x8plus_minus_1_out_13, x8plus_minus_1_out_14, x8plus_minus_1_out_15, x8plus_minus_1_out_16,
       x8plus_minus_1_out_17, x8plus_minus_1_out_18;
  wire [7:0] and_1_out, and_2_out, and_3_out, bit_extender_1_out, bit_extender_2_out, bit_extender_3_out,
       not_3_out, or_2_out, ram_1_dout, x8counter_1_out_17;
  wire [15:0] adresse_map_1_b1;

  not not_1 (not_1_out, WRITE);
  not not_2 (not_2_out, RESETTONULL);
  or or_1 (or_1_out, UPDATERAM, RESETTO0);
  assign not_3_out = ~bit_extender_1_out;  // NOT_Gate not_3, 8 bits wide
  not not_4 (not_4_out, RESETTO0);
  assign or_2_out = and_1_out | and_2_out;  // OR_Gate or_2, 8 bits wide
  assign and_1_out = {A65355, in_9, in_10, in_11, in_12, in_13, in_14, A1} & not_3_out;  // AND_Gate and_1, 8 bits wide
  assign and_2_out = bit_extender_1_out & x8counter_1_out_17;  // AND_Gate and_2, 8 bits wide
  assign bit_extender_1_out = {{7{not_1_out}}, not_1_out};  // Bit_Extender bit_extender_1
  assign bit_extender_2_out = {{7{not_4_out}}, not_4_out};  // Bit_Extender bit_extender_2
  assign and_3_out = bit_extender_2_out & or_2_out;  // AND_Gate and_3, 8 bits wide
  ADRESSE_MAP adresse_map_1 (
    .NEXT_CELL(NEXTCELL), .PREVIOUS_CELL(PREVCELL), .UPDATE(UPDATEREGS), .B65536(adresse_map_1_b1[15]),
    .out_5(adresse_map_1_b1[14]), .out_6(adresse_map_1_b1[13]), .out_7(adresse_map_1_b1[12]),
    .out_8(adresse_map_1_b1[11]), .out_9(adresse_map_1_b1[10]), .out_10(adresse_map_1_b1[9]),
    .out_11(adresse_map_1_b1[8]), .out_12(adresse_map_1_b1[7]), .out_13(adresse_map_1_b1[6]),
    .out_14(adresse_map_1_b1[5]), .out_15(adresse_map_1_b1[4]), .out_16(adresse_map_1_b1[3]),
    .out_17(adresse_map_1_b1[2]), .out_18(adresse_map_1_b1[1]), .B1(adresse_map_1_b1[0]));  // open: OVERFLOW
  x8PLUS_MINUS x8plus_minus_1 (
    .A128(ram_1_dout[7]), .in_2(ram_1_dout[6]), .in_3(ram_1_dout[5]), .in_4(ram_1_dout[4]),
    .in_5(ram_1_dout[3]), .in_6(ram_1_dout[2]), .in_7(ram_1_dout[1]), .A1(ram_1_dout[0]), .PLUS(PLUS),
    .MINUS(MINUS), .B128(x8plus_minus_1_b128), .out_13(x8plus_minus_1_out_13),
    .out_14(x8plus_minus_1_out_14), .out_15(x8plus_minus_1_out_15), .out_16(x8plus_minus_1_out_16),
    .out_17(x8plus_minus_1_out_17), .out_18(x8plus_minus_1_out_18), .B1(x8plus_minus_1_b1));  // open: OVERFLOW
  RAM #(.addrWidth(16), .trigger("high")) ram_1 (
    .addr(adresse_map_1_b1), .we(or_1_out), .din(and_3_out), .dout(ram_1_dout));  // open: oe
  x8COUNTER x8counter_1 (
    .in_1(x8plus_minus_1_b128), .in_2(x8plus_minus_1_out_13), .in_3(x8plus_minus_1_out_14),
    .in_4(x8plus_minus_1_out_15), .in_5(x8plus_minus_1_out_16), .in_6(x8plus_minus_1_out_17),
    .in_7(x8plus_minus_1_out_18), .in_8(x8plus_minus_1_b1), .UPDATE(UPDATEREGS),
    .out_10(x8counter_1_out_17[7]), .out_11(x8counter_1_out_17[6]), .out_12(x8counter_1_out_17[5]),
    .out_13(x8counter_1_out_17[4]), .out_14(x8counter_1_out_17[3]), .out_15(x8counter_1_out_17[2]),
    .out_16(x8counter_1_out_17[1]), .out_17(x8counter_1_out_17[0]));
  assign bit_extender_3_out = {{7{READ}}, READ};  // Bit_Extender bit_extender_3
  assign {B128, out_20, out_21, out_22, out_23, out_24, out_25, B1} = bit_extender_3_out & ram_1_dout;  // AND_Gate and_4, 8 bits wide

  assign READED = READ;
endmodule

module PATH_DIVIDER (
  input  BPClock,
  input  CLOCK,
  input  ROM3,
  input  in_4,
  input  ROM1,
  input  BUTTON,
  input  VALID,
  output STOPCLOCK,
  output REDIRECTCLOCK,
  output ROMPLUS1,
  output REFRESHROM,
  output ROMMINUS1,
  output PLUS1,
  output MINUS1,
  output NEXTREG,
  output PREVREG,
  output UPDATERAMREG,
  output UPDATERAMVALUE,
  output GETRAM,
  output UPDATESCREEN,
  output RAMREADYTOWRITE
);

  wire and_1_out, and_2_out, and_3_out, and_4_out, and_5_out, and_6_out, and_7_out, and_8_out, and_9_out,
       and_10_out, and_11_out, and_12_out, and_13_out, and_14_out, and_15_out, and_16_out, and_17_out,
       and_18_out, and_19_out, and_21_out, and_28_out, and_31_out, and_32_out, and_33_out, and_34_out,
       and_35_out, and_36_out, bracket_logic_1_valid, d_ff_1_q, d_ff_2_q, d_ff_3_q, d_ff_4_q, d_ff_5_q,
       d_ff_6_q, d_ff_7_q, d_ff_8_q, d_ff_9_q, d_ff_10_q, d_ff_11_q, d_ff_12_q, nor_1_out, nor_2_out,
       not_1_out, not_2_out, not_3_out, not_4_out, not_5_out, not_6_out, not_7_out, not_8_out, not_9_out,
       not_10_out, not_11_out, not_12_out, not_13_out, or_1_out, or_2_out, or_3_out, or_4_out, or_5_out,
       or_6_out, or_7_out, or_8_out, or_9_out, or_10_out, or_11_out, or_12_out, or_13_out;

  or or_1 (or_1_out, or_2_out, d_ff_1_q);
  not not_1 (not_1_out, or_1_out);
  D_Flip_Flop d_ff_1 (.D(not_1_out), .clk(and_1_out), .Q(d_ff_1_q));  // open: Qn, preset, reset
  and and_1 (and_1_out, not_2_out, CLOCK);
  not not_2 (not_2_out, BPClock);
  or or_2 (or_2_out, d_ff_3_q, d_ff_2_q);
  D_Flip_Flop d_ff_2 (.D(d_ff_1_q), .clk(and_1_out), .Q(d_ff_2_q));  // open: Qn, preset, reset
  and and_2 (and_2_out, CLOCK, BPClock);
  D_Flip_Flop d_ff_3 (.D(d_ff_2_q), .clk(and_1_out), .Q(d_ff_3_q));  // open: Qn, preset, reset
  and and_3 (and_3_out, and_2_out, and_16_out);
  and and_4 (and_4_out, in_4, ROM1);
  D_Flip_Flop d_ff_4 (.D(d_ff_3_q), .clk(and_1_out), .Q(d_ff_4_q));  // open: Qn, preset, reset
  or or_3 (or_3_out, or_9_out, d_ff_5_q);
  not not_3 (not_3_out, or_3_out);
  D_Flip_Flop d_ff_5 (.D(not_3_out), .clk(or_4_out), .Q(d_ff_5_q));  // open: Qn, preset, reset
  or or_4 (or_4_out, d_ff_1_q, and_3_out);
  or or_5 (or_5_out, d_ff_1_q, d_ff_4_q);
  or or_6 (or_6_out, d_ff_2_q, d_ff_3_q);
  or or_7 (or_7_out, d_ff_3_q, d_ff_4_q);
  or or_8 (or_8_out, d_ff_2_q, and_34_out);
  or or_9 (or_9_out, d_ff_11_q, d_ff_7_q);
  LED led_1 (.in(d_ff_5_q));
  not not_4 (not_4_out, or_5_out);
  not not_5 (not_5_out, ROM3);
  D_Flip_Flop d_ff_6 (.D(VALID), .clk(or_8_out), .Q(d_ff_6_q));  // open: Qn, preset, reset
  D_Flip_Flop d_ff_7 (.D(and_5_out), .clk(or_4_out), .Q(d_ff_7_q));  // open: Qn, preset, reset
  and and_5 (and_5_out, d_ff_5_q, not_4_out);
  and and_6 (and_6_out, not_5_out, and_4_out);
  and and_7 (and_7_out, ROM3, and_4_out);
  D_Flip_Flop d_ff_8 (.D(ROM3), .clk(d_ff_1_q), .Q(d_ff_8_q));  // open: Qn, preset, reset
  D_Flip_Flop d_ff_9 (.D(in_4), .clk(d_ff_1_q), .Q(d_ff_9_q));  // open: Qn, preset, reset
  D_Flip_Flop d_ff_10 (.D(ROM1), .clk(d_ff_1_q), .Q(d_ff_10_q));  // open: Qn, preset, reset
  D_Flip_Flop d_ff_11 (.D(and_8_out), .clk(or_4_out), .Q(d_ff_11_q));  // open: Qn, preset, reset
  and and_8 (and_8_out, d_ff_7_q, not_4_out);
  not not_6 (not_6_out, d_ff_10_q);
  nor nor_1 (nor_1_out, d_ff_8_q, d_ff_9_q);
  not not_7 (not_7_out, BUTTON);
  not not_8 (not_8_out, d_ff_9_q);
  nor nor_2 (nor_2_out, d_ff_9_q, d_ff_10_q);
  and and_9 (and_9_out, d_ff_9_q, not_6_out);
  and and_10 (and_10_out, nor_1_out, d_ff_10_q);
  and and_11 (and_11_out, d_ff_8_q, not_8_out);
  and and_12 (and_12_out, d_ff_9_q, d_ff_10_q);
  and and_13 (and_13_out, d_ff_6_q, d_ff_2_q);
  D_Flip_Flop d_ff_12 (.D(and_14_out), .clk(or_4_out), .Q(d_ff_12_q));  // open: Qn, preset, reset
  and and_14 (and_14_out, d_ff_11_q, not_4_out);
  and and_15 (and_15_out, and_11_out, d_ff_10_q);
  and and_16 (and_16_out, and_12_out, d_ff_6_q);
  LED led_2 (.in(d_ff_7_q));
  LED led_3 (.in(d_ff_11_q));
  LED led_4 (.in(d_ff_12_q));
  and and_17 (and_17_out, not_7_out, and_15_out);
  not not_9 (not_9_out, d_ff_8_q);
  not not_10 (not_10_out, d_ff_8_q);
  and and_18 (and_18_out, or_6_out, nor_2_out);
  not not_11 (not_11_out, d_ff_8_q);
  and and_19 (and_19_out, or_6_out, and_9_out);
  or or_10 (or_10_out, and_9_out, nor_2_out);
  or or_11 (or_11_out, nor_2_out, and_15_out);
  and and_20 (STOPCLOCK, d_ff_2_q, and_17_out);
  and and_21 (and_21_out, and_16_out, not_9_out);
  and and_22 (PLUS1, not_10_out, and_18_out);
  and and_23 (MINUS1, and_18_out, d_ff_8_q);
  and and_24 (NEXTREG, not_11_out, and_19_out);
  and and_25 (PREVREG, and_19_out, d_ff_8_q);
  and and_26 (UPDATERAMREG, or_10_out, d_ff_3_q);
  and and_27 (UPDATERAMVALUE, or_11_out, d_ff_4_q);
  and and_28 (and_28_out, or_6_out, and_10_out);
  and and_29 (UPDATESCREEN, d_ff_3_q, and_10_out);
  and and_30 (RAMREADYTOWRITE, or_7_out, and_15_out);
  or or_12 (or_12_out, or_6_out, d_ff_1_q);
  and and_31 (and_31_out, or_12_out, and_12_out);
  and and_32 (and_32_out, and_12_out, and_13_out);
  or or_13 (or_13_out, d_ff_3_q, d_ff_4_q);
  not not_12 (not_12_out, and_16_out);
  or or_14 (GETRAM, and_28_out, and_31_out);
  or or_15 (ROMPLUS1, and_21_out, and_33_out);
  and and_33 (and_33_out, or_13_out, not_12_out);
  BRACKET_LOGIC bracket_logic_1 (.UPDATE(d_ff_7_q), .MORE(and_6_out), .LESS(and_7_out), .VALID(bracket_logic_1_valid));
  and and_34 (and_34_out, d_ff_11_q, bracket_logic_1_valid);
  and and_35 (and_35_out, d_ff_12_q, and_16_out);
  and and_36 (and_36_out, and_16_out, d_ff_8_q);
  not not_13 (not_13_out, and_34_out);
  or or_16 (REFRESHROM, and_35_out, d_ff_4_q);
  LED led_5 (.in(STOPCLOCK));
  and and_37 (REDIRECTCLOCK, not_13_out, and_32_out);
  LED led_6 (.in(REDIRECTCLOCK));
  LED led_7 (.in(ROMPLUS1));
  LED led_8 (.in(REFRESHROM));
  and and_38 (ROMMINUS1, not_13_out, and_36_out);
  LED led_9 (.in(ROMMINUS1));
  LED led_10 (.in(PLUS1));
  LED led_11 (.in(MINUS1));
  LED led_12 (.in(NEXTREG));
  LED led_13 (.in(PREVREG));
  LED led_14 (.in(UPDATERAMREG));
  LED led_15 (.in(UPDATERAMVALUE));
  LED led_16 (.in(GETRAM));
  LED led_17 (.in(UPDATESCREEN));
  LED led_18 (.in(RAMREADYTOWRITE));
endmodule

module V2 (
);

  wire and_1_out, bracket_check_1_yes, button_1_out, clock_1_out, not_1_out, not_2_out,
       path_divider_1_getram, path_divider_1_minus1, path_divider_1_nextreg, path_divider_1_plus1,
       path_divider_1_prevreg, path_divider_1_ramreadytowrite, path_divider_1_redirectclock,
       path_divider_1_stopclock, path_divider_1_updateramreg, path_divider_1_updateramvalue,
       path_divider_1_updatescreen, RESETCELLVALUE_out, RESETRAMCOUNTER_out, RESETSCREEN_out,
       rom_archi_1_ins1, rom_archi_1_ins2, rom_archi_1_ins3;
  wire [0:0] ram_archi_1_b128;
  wire [2:0] path_divider_1_romplus1;
  wire [6:0] ram_archi_1_b1;
  wire [7:0] undriven;

  Clock clock_1 (.out(clock_1_out));
  and and_1 (and_1_out, not_1_out, clock_1_out);
  not not_1 (not_1_out, path_divider_1_stopclock);
  ROM_ARCHI rom_archi_1 (
    .NEXTINS(path_divider_1_romplus1[0]), .UPDATE(path_divider_1_romplus1[1]),
    .PREVIOUSINS(path_divider_1_romplus1[2]), .INS1(rom_archi_1_ins1), .INS2(rom_archi_1_ins2),
    .INS3(rom_archi_1_ins3));
  not not_2 (not_2_out, rom_archi_1_ins1);
  Button button_1 (.out(button_1_out));
  // DipSwitch dipswitch_1: pin names not known
  PATH_DIVIDER path_divider_1 (
    .BPClock(path_divider_1_redirectclock), .CLOCK(and_1_out), .ROM3(rom_archi_1_ins1),
    .in_4(rom_archi_1_ins2), .ROM1(rom_archi_1_ins3), .BUTTON(button_1_out), .VALID(bracket_check_1_yes),
    .STOPCLOCK(path_divider_1_stopclock), .REDIRECTCLOCK(path_divider_1_redirectclock),
    .ROMPLUS1(path_divider_1_romplus1[0]), .REFRESHROM(path_divider_1_romplus1[1]),
    .ROMMINUS1(path_divider_1_romplus1[2]), .PLUS1(path_divider_1_plus1), .MINUS1(path_divider_1_minus1),
    .NEXTREG(path_divider_1_nextreg), .PREVREG(path_divider_1_prevreg),
    .UPDATERAMREG(path_divider_1_updateramreg), .UPDATERAMVALUE(path_divider_1_updateramvalue),
    .GETRAM(path_divider_1_getram), .UPDATESCREEN(path_divider_1_updatescreen),
    .RAMREADYTOWRITE(path_divider_1_ramreadytowrite));
  BRACKET_CHECK bracket_check_1 (
    .A128(ram_archi_1_b128[0]), .in_2(ram_archi_1_b1[6]), .in_3(ram_archi_1_b1[5]), .in_4(ram_archi_1_b1[4]),
    .in_5(ram_archi_1_b1[3]), .in_6(ram_archi_1_b1[2]), .in_7(ram_archi_1_b1[1]), .A1(ram_archi_1_b1[0]),
    .FORWARD_if1(not_2_out), .YES(bracket_check_1_yes));  // open: SKIP
  Button RESETRAMCOUNTER (.out(RESETRAMCOUNTER_out));
  Button RESETCELLVALUE (.out(RESETCELLVALUE_out));
  RAM_ARCHI ram_archi_1 (
    .READ(path_divider_1_getram), .NEXTCELL(path_divider_1_nextreg), .PREVCELL(path_divider_1_prevreg),
    .RESETTONULL(RESETRAMCOUNTER_out), .UPDATEREGS(path_divider_1_updateramreg),
    .UPDATERAM(path_divider_1_updateramvalue), .RESETTO0(RESETCELLVALUE_out), .A65355(undriven[7]),
    .in_9(undriven[6]), .in_10(undriven[5]), .in_11(undriven[4]), .in_12(undriven[3]), .in_13(undriven[2]),
    .in_14(undriven[1]), .A1(undriven[0]), .PLUS(path_divider_1_plus1), .MINUS(path_divider_1_minus1),
    .WRITE(path_divider_1_ramreadytowrite), .B128(ram_archi_1_b128[0]), .out_20(ram_archi_1_b1[6]),
    .out_21(ram_archi_1_b1[5]), .out_22(ram_archi_1_b1[4]), .out_23(ram_archi_1_b1[3]),
    .out_24(ram_archi_1_b1[2]), .out_25(ram_archi_1_b1[1]), .B1(ram_archi_1_b1[0]));  // open: READED
  TTY #(.trigger("falling")) tty_1 (
    .data(ram_archi_1_b1), .clk(path_divider_1_updatescreen), .we(1'b1), .clr(RESETSCREEN_out));
  Button RESETSCREEN (.out(RESETSCREEN_out));

  // Notes on the sheet:
  //   INPUT
  //   OUTPUT
endmodule
